# Fritzing sketch SaxCircuit2 (saved by Fritzing 0.9.3b)
stripboards: 1

parts:
  Brain = Arduino Micro (Rev3)
  VCC1 = Battery block 9V
  Speed = Pushbutton [package="[THT]"]
  Mode = Pushbutton [package="[THT]"]
  LED1 = RGB LED - (4 legs) [package="5 mm [THT]"]
  LED2 = RGB LED - (4 legs) [package="5 mm [THT]"]
  R1 = Resistor [tolerance=±5% resistance=220 package=THT]
  R2 = Resistor [tolerance=±5% resistance=220 package=THT]
  Q7 = MOSFET-NCHANNEL [package=to220v]
  Q8 = MOSFET-NCHANNEL [package=to220v]
  Q9 = MOSFET-NCHANNEL [package=to220v]
  Q10 = MOSFET-NCHANNEL [package=to220v]
  Q11 = MOSFET-NCHANNEL [package=to220v]
  Q12 = MOSFET-NCHANNEL [package=to220v]
  R3 = Resistor [tolerance=±5% resistance=10k package=THT]
  R4 = Resistor [tolerance=±5% resistance=10k package=THT]
  R5 = Resistor [tolerance=±5% resistance=10k package=THT]
  R6 = Resistor [tolerance=±5% resistance=10k package=THT]
  R7 = Resistor [tolerance=±5% resistance=10k package=THT]
  R8 = Resistor [tolerance=±5% resistance=10k package=THT]
  VCC2 = 4 x AAA Battery Mount
  Spare = Pushbutton [package="[THT]"]
  R9 = Resistor [tolerance=±5% resistance=220 package=THT]

nets:
  N1: Brain.GND, VCC1.-, R1.Pin_0, R2.Pin_0, Q7.S, Q8.S, Q9.S, Q10.S, Q11.S, Q12.S, R3.Pin_1, R4.Pin_1, R5.Pin_1, R6.Pin_1, R7.Pin_1, R8.Pin_1, VCC2.-, R9.Pin_0
  N2: Brain.D5_PWM, Mode.Pin_3, Mode.Pin_4, R1.Pin_1
  N3: Brain.D6_PWM/A7, Speed.Pin_3, Speed.Pin_4, R2.Pin_1
  N4: Brain.D7, Spare.Pin_2, R9.Pin_1
  N5: Brain.D8_PWM/A8, Q12.G, R5.Pin_0
  N6: Brain.D9_PWM/A9, Q11.G, R6.Pin_0
  N7: Brain.D10_PWM/A10, Q10.G, R3.Pin_0
  N8: Brain.D11_PWM, Q9.G, R8.Pin_0
  N9: Brain.D12_PWM/A11, Q8.G, R7.Pin_0
  N10: Brain.VIN, Speed.Pin_1, Speed.Pin_2, Mode.Pin_1, Mode.Pin_2, VCC2.+, Spare.Pin_3
  N11: Brain.D13_PWM, Q7.G, R4.Pin_0
  N12: VCC1.+, LED1.common_anode, LED2.common_anode
  N13: LED1.red_cathode, Q7.D
  N14: LED1.green_cathode, Q8.D
  N15: LED1.blue_cathode, Q9.D
  N16: LED2.red_cathode, Q10.D
  N17: LED2.green_cathode, Q11.D
  N18: LED2.blue_cathode, Q12.D
